// Logisim project arithmetic-ALU1.circ as structural Verilog
module Full_Adder (
  input  A,
  input  B,
  input  Cin,
  output Sum,
  output Cout
);

  wire and_1_out, and_2_out, and_3_out, and_4_out, and_5_out, and_6_out, and_7_out, not_1_out, not_2_out,
       not_3_out, or_1_out, or_2_out, or_3_out;

  not not_1 (not_1_out, A);
  not not_2 (not_2_out, B);
  not not_3 (not_3_out, Cin);
  and and_1 (and_1_out, Cin, B);
  or or_1 (or_1_out, Cin, B);
  and and_2 (and_2_out, Cin, not_2_out);
  and and_3 (and_3_out, B, not_3_out);
  and and_4 (and_4_out, not_2_out, not_3_out);
  and and_5 (and_5_out, or_1_out, A);
  or or_2 (or_2_out, and_2_out, and_3_out);
  or or_3 (or_3_out, and_4_out, and_1_out);
  or or_4 (Cout, and_1_out, and_5_out);
  and and_6 (and_6_out, not_1_out, or_2_out);
  and and_7 (and_7_out, A, or_3_out);
  or or_5 (Sum, and_6_out, and_7_out);
endmodule

module _4_Bits_Adder (
  input  in_1,
  input  in_2,
  input  in_3,
  input  in_4,
  input  in_5,
  input  in_6,
  input  in_7,
  input  in_8,
  input  in_9,
  output out_10,
  output out_11,
  output out_12,
  output out_13,
  output out_14
);

  wire full_adder_2_cout, full_adder_3_cout, full_adder_4_cout;

  Full_Adder full_adder_1 (.A(in_1), .B(in_2), .Cin(full_adder_2_cout), .Sum(out_11), .Cout(out_10));
  Full_Adder full_adder_2 (.A(in_3), .B(in_4), .Cin(full_adder_3_cout), .Sum(out_12), .Cout(full_adder_2_cout));
  Full_Adder full_adder_3 (.A(in_5), .B(in_6), .Cin(full_adder_4_cout), .Sum(out_13), .Cout(full_adder_3_cout));
  Full_Adder full_adder_4 (.A(in_7), .B(in_8), .Cin(in_9), .Sum(out_14), .Cout(full_adder_4_cout));
endmodule

module _8_Bits_Adder (
  input  in_1,
  input  in_2,
  input  in_3,
  input  in_4,
  input  in_5,
  input  in_6,
  input  in_7,
  input  in_8,
  input  in_9,
  input  in_10,
  input  in_11,
  input  in_12,
  input  in_13,
  input  in_14,
  input  in_15,
  input  in_16,
  input  in_17,
  output out_18,
  output out_19,
  output out_20,
  output out_21,
  output out_22,
  output out_23,
  output out_24,
  output out_25,
  output out_26
);

  wire n4_bits_adder_2_out_10;

  _4_Bits_Adder u_4_bits_adder_1 (
    .in_1(in_1), .in_2(in_2), .in_3(in_3), .in_4(in_4), .in_5(in_5), .in_6(in_6), .in_7(in_7), .in_8(in_8),
    .out_11(out_19), .out_12(out_20), .out_13(out_21), .out_14(out_22), .out_10(out_18),
    .in_9(n4_bits_adder_2_out_10));
  _4_Bits_Adder u_4_bits_adder_2 (
    .in_1(in_9), .in_2(in_10), .in_3(in_11), .in_4(in_12), .in_5(in_13), .in_6(in_14), .in_7(in_15),
    .in_8(in_16), .out_11(out_23), .out_12(out_24), .out_13(out_25), .out_14(out_26),
    .out_10(n4_bits_adder_2_out_10), .in_9(in_17));
endmodule

module _4_Bits_EXOR_Gate_IC (
  input  in_1,
  input  in_2,
  input  in_3,
  input  in_4,
  input  in_5,
  input  in_6,
  input  in_7,
  input  in_8,
  output out_9,
  output out_10,
  output out_11,
  output out_12
);

  wire and_1_out, and_2_out, and_3_out, and_4_out, and_5_out, and_6_out, and_7_out, and_8_out, not_1_out,
       not_2_out, not_3_out, not_4_out, not_5_out, not_6_out, not_7_out, not_8_out;

  not not_1 (not_1_out, in_1);
  not not_2 (not_2_out, in_2);
  not not_3 (not_3_out, in_3);
  not not_4 (not_4_out, in_4);
  not not_5 (not_5_out, in_5);
  not not_6 (not_6_out, in_6);
  not not_7 (not_7_out, in_7);
  not not_8 (not_8_out, in_8);
  and and_1 (and_1_out, not_1_out, in_2);
  and and_2 (and_2_out, in_1, not_2_out);
  and and_3 (and_3_out, not_3_out, in_4);
  and and_4 (and_4_out, in_3, not_4_out);
  and and_5 (and_5_out, not_5_out, in_6);
  and and_6 (and_6_out, in_5, not_6_out);
  and and_7 (and_7_out, not_7_out, in_8);
  and and_8 (and_8_out, in_7, not_8_out);
  or or_1 (out_9, and_1_out, and_2_out);
  or or_2 (out_10, and_3_out, and_4_out);
  or or_3 (out_11, and_5_out, and_6_out);
  or or_4 (out_12, and_7_out, and_8_out);
endmodule

module AdderSubstract (
  input  Substract,
  input  B7,
  input  B6,
  input  B5,
  input  B4,
  input  B3,
  input  B2,
  input  B1,
  input  B0,
  input  A7,
  input  A6,
  input  A5,
  input  A4,
  input  A3,
  input  A2,
  input  A1,
  input  A0,
  output _128,
  output _64,
  output _32,
  output _16,
  output _8,
  output _4,
  output _2,
  output _1,
  output _256
);

  wire n4_bits_exor_ic_1_out_9, n4_bits_exor_ic_1_out_10, n4_bits_exor_ic_1_out_11, n4_bits_exor_ic_1_out_12,
       n4_bits_exor_ic_2_out_9, n4_bits_exor_ic_2_out_10, n4_bits_exor_ic_2_out_11, n4_bits_exor_ic_2_out_12,
       n8_bits_adder_1_out_18, not_1_out;

  and and_1 (_256, n8_bits_adder_1_out_18, not_1_out);
  not not_1 (not_1_out, Substract);
  _8_Bits_Adder u_8_bits_adder_1 (
    .in_1(A7), .in_2(n4_bits_exor_ic_1_out_9), .in_3(A6), .in_4(n4_bits_exor_ic_1_out_10), .in_5(A5),
    .in_6(n4_bits_exor_ic_1_out_11), .in_7(A4), .in_8(n4_bits_exor_ic_1_out_12), .in_9(A3),
    .in_10(n4_bits_exor_ic_2_out_9), .in_11(A2), .in_12(n4_bits_exor_ic_2_out_10), .in_13(A1),
    .in_14(n4_bits_exor_ic_2_out_11), .in_15(A0), .in_16(n4_bits_exor_ic_2_out_12), .out_19(_128),
    .out_20(_64), .out_21(_32), .out_22(_16), .out_23(_8), .out_24(_4), .out_25(_2), .out_26(_1),
    .out_18(n8_bits_adder_1_out_18), .in_17(Substract));
  _4_Bits_EXOR_Gate_IC u_4_bits_exor_ic_1 (
    .in_1(B7), .in_2(Substract), .in_3(B6), .in_4(Substract), .in_5(B5), .in_6(Substract), .in_7(B4),
    .in_8(Substract), .out_9(n4_bits_exor_ic_1_out_9), .out_10(n4_bits_exor_ic_1_out_10),
    .out_11(n4_bits_exor_ic_1_out_11), .out_12(n4_bits_exor_ic_1_out_12));
  _4_Bits_EXOR_Gate_IC u_4_bits_exor_ic_2 (
    .in_1(B3), .in_2(Substract), .in_3(B2), .in_4(Substract), .in_5(B1), .in_6(Substract), .in_7(B0),
    .in_8(Substract), .out_9(n4_bits_exor_ic_2_out_9), .out_10(n4_bits_exor_ic_2_out_10),
    .out_11(n4_bits_exor_ic_2_out_11), .out_12(n4_bits_exor_ic_2_out_12));
  Hex_Digit_Display hex_digit_display_1 (.value({_128, _64, _32, _16}));  // open: dp
  Hex_Digit_Display hex_digit_display_2 (.value({_8, _4, _2, _1}));  // open: dp

  // Notes on the sheet:
  //   16 x
  //   x 1
endmodule
